// Digital circuit alu-extended.dig as structural Verilog
module alu_extended (
  input  [15:0] A,
  input  [15:0] B,
  input  [2:0] ALUOP,
  input  D,
  input  ALUIMM,
  output [15:0] RESULT,
  output [3:0] FLAG
);

  wire add_1_c_o, and_2_out, multiplexer_6_out, nand_1_out, not_3_out, or_2_out, or_3_out, xnor_1_out,
       xor_2_out;
  wire [15:0] add_1_s, and_1_out, barrel_shift_1_result, multiplexer_1_out, multiplexer_2_out, neg_1_out,
       not_1_out, not_2_out, or_1_out, xor_1_out;

  assign not_1_out = ~B;  // Not not_1, 16 bits wide
  Multiplexer #(.Bits(16)) multiplexer_1 (.sel(ALUOP[0]), .in_0(B), .in_1(not_1_out), .out(multiplexer_1_out));
  assign and_1_out = A & B;  // And and_1, 16 bits wide
  assign or_1_out = A | B;  // Or or_1, 16 bits wide
  assign xor_1_out = A ^ B;  // XOr xor_1, 16 bits wide
  assign not_2_out = ~A;  // Not not_2, 16 bits wide
  barrel_shift barrel_shift_1 (.A(A), .B(B), .D(D), .RESULT(barrel_shift_1_result));
  Neg #(.Bits(16)) neg_1 (.in(A), .out(neg_1_out));
  Add #(.Bits(16)) add_1 (.a(A), .b(multiplexer_1_out), .c_i(ALUOP[0]), .s(add_1_s), .c_o(add_1_c_o));
  xnor xnor_1 (xnor_1_out, multiplexer_1_out[15], A[15]);
  xor xor_2 (xor_2_out, A[15], add_1_s[15]);
  Multiplexer #(.Selector_Bits(3), .Bits(16)) multiplexer_2 (
    .sel(ALUOP), .in_0(add_1_s), .in_1(add_1_s), .in_2(and_1_out), .in_3(or_1_out), .in_4(xor_1_out),
    .in_5(not_2_out), .in_6(barrel_shift_1_result), .in_7(neg_1_out), .out(multiplexer_2_out));
  Multiplexer #(.Bits(16)) multiplexer_3 (
    .sel(not_3_out), .in_0(add_1_s), .in_1(multiplexer_2_out), .out({FLAG[1], RESULT[14:0]}));
  and and_2 (and_2_out, xnor_1_out, xor_2_out);
  not not_3 (not_3_out, ALUIMM);
  Multiplexer multiplexer_4 (.sel(multiplexer_6_out), .in_0(and_2_out), .in_1(1'b0), .out(FLAG[3]));
  Multiplexer multiplexer_5 (.sel(multiplexer_6_out), .in_0(add_1_c_o), .in_1(1'b0), .out(FLAG[2]));
  or or_2 (or_2_out, RESULT[0], RESULT[1], RESULT[2], RESULT[3], RESULT[4], RESULT[5], RESULT[6], RESULT[7], RESULT[8], RESULT[9], RESULT[10], RESULT[11], RESULT[12], RESULT[13], RESULT[14], FLAG[1]);
  Multiplexer multiplexer_6 (.sel(nand_1_out), .in_0(1'b0), .in_1(or_3_out), .out(multiplexer_6_out));
  not not_4 (FLAG[0], or_2_out);
  // NotConnected on nothing
  // NotConnected on nothing
  or or_3 (or_3_out, ALUOP[1], ALUOP[2]);
  nand nand_1 (nand_1_out, ALUOP[2], ALUOP[1], ALUOP[0]);

  assign RESULT[15] = FLAG[1];

  // Other names for the same wires on the sheet: IMM = ALUIMM; S[2:0] = ALUOP; S0 = ALUOP[0]; S1 = ALUOP[1];
  //   S2 = ALUOP[2]

  // Notes on the sheet:
  //   A: First input to ALU
  //   B: Second input to ALU
  //   ALUOP: Operation selection input
  //   RESULT: The result of this ALU operation
  //   FLAG: The flags associated with the result of this ALU operation
  //   0. Z (zero)
  //   1. N (negative)
  //   2. C (carry)
  //   3. V (overflow)
  //   D: The direction for the shifts
  //   ALUIMM: if immediate action
  //   Arithmetic logic
  //   Non-Arithmetic logic
  //   Overflow flag logic
  //   If the IMM bit is low, then its a ALU IMM instruction which starts with 0. Then just choose the add/sub method
  //   Carry flag logic
  //   Zero & Negative flag logic
  //   Z
  //   N
  //   No overflow or carry on anything but 001, 000 or 111
  //   V
  //   C
endmodule
