// Digital circuit control_unit-extended.dig as structural Verilog
module control_unit_extended (
  input  [15:0] INST,
  input  ZREG,
  output [2:0] ALUOP,
  output [2:0] RS1,
  output [2:0] RS2,
  output [2:0] WS,
  output STR,
  output WE,
  output [1:0] DMUX,
  output LDR,
  output FLEN,
  output SETH,
  output D
);

  wire and_1_out, and_3_out, nand_1_out, not_1_out, not_2_out, not_3_out, not_4_out, not_6_out, not_7_out,
       not_8_out, not_10_out, not_11_out, not_12_out;

  not not_1 (not_1_out, ZREG);
  nand nand_1 (nand_1_out, not_1_out, INST[11]);
  not not_2 (not_2_out, INST[12]);
  not not_3 (not_3_out, INST[13]);
  not not_4 (not_4_out, INST[14]);
  not not_5 (not_4_out, INST[14]);
  not not_6 (not_6_out, INST[15]);
  not not_7 (not_7_out, INST[13]);
  not not_8 (not_8_out, INST[14]);
  not not_9 (not_8_out, INST[14]);
  not not_10 (not_10_out, INST[15]);
  not not_11 (not_11_out, INST[14]);
  Multiplexer #(.Bits(3)) multiplexer_1 (.sel(INST[14]), .in_0(INST[2:0]), .in_1(INST[10:8]), .out(RS2));
  not not_12 (not_12_out, INST[12]);
  and and_1 (and_1_out, not_12_out, INST[14]);
  and and_2 (DMUX[0], INST[14], INST[12]);
  and and_3 (and_3_out, not_2_out, not_3_out, not_4_out, not_6_out);
  and and_4 (SETH, INST[12], not_7_out, not_8_out, not_10_out);
  and and_5 (FLEN, not_11_out, INST[15]);
  Multiplexer #(.Bits(3)) multiplexer_2 (.sel(nand_1_out), .in_0(3'b000), .in_1(INST[10:8]), .out(WS));
  and and_6 (STR, nand_1_out, and_1_out);
  or or_1 (DMUX[1], and_3_out, SETH);
  not not_13 (WE, STR);
  LED led_1 (.in(nand_1_out));
  // NotConnected on nothing
  // NotConnected on nothing
  // NotConnected on nothing
  // NotConnected on nothing
  // NotConnected on nothing
  // NotConnected on nothing
  // NotConnected on nothing
  // NotConnected on nothing
  // NotConnected on nothing
  // NotConnected on nothing
  // Pins of 2 and 3 bits meet at INST[14:12]

  assign ALUOP = INST[14:12];
  assign D = INST[3];
  assign LDR = 1'b1;
  assign RS1 = INST[6:4];

  // Notes on the sheet:
  //   FLEN: Checks whether the flag register should be written to or not
  //   only on ALU OP codes (1 0 x x)
  //   ZREG: ALU Flag
  //   SETH: the SETH instruction
  //   D: The direction for the Logical shift
  //   Z
  //   Rd
  //   Ra
  //   Rb
  //   opcode
  //   D
  //   Testing for LDR
  //   Testing for MOV
  //   Testing for SETH
  //   Choose zero register to write if cond == false
endmodule

/* Test case All Tests:
	INST                                    WE  ALUOP  RS1   RS2  WS  STR  LDR DMUX

let aluop  = 0b1000;
let ldrop  = 0b0101;
let strop  = 0b0100;
let movlop = 0b0000;

loop(rd, 1<<3)
loop(ra, 1<<3)
loop(rb, 1<<3)

loop(i, 4)
	((aluop+i)<<12 | rd<<8 | ra<<4 | rb<<0) 1  (i)     (ra)  (rb) (rd)  0   X    0  #test add/sub/and/orr
end loop

	(ldrop    <<12 | rd<<8 | ra<<4 )        1  X       (ra)  x    (rd)  0   1    1  #test ldr
	(strop    <<12 | rd<<8 | ra<<4 )        0  X       (ra)  (rd)  X    1   X    X  #test str
	
	let imm = random(256);
	(movlop   <<12 | rd<<8 | imm )          1  X       X      X   (rd)  0   X    2  #test movl

end loop
end loop
end loop
*/

/* Test case WS:
	INST                                    WS 

let aluop  = 0b1000;
let ldrop  = 0b0101;
let strop  = 0b0100;
let movlop = 0b0000;

loop(rd, 1<<3)
loop(ra, 1<<3)
loop(rb, 1<<3)

loop(i, 4)
	((aluop+i)<<12 | rd<<8 | ra<<4 | rb<<0) (rd)  #test add/sub/and/orr
end loop

	(ldrop    <<12 | rd<<8 | ra<<4 )        (rd)   #test ldr
	(strop    <<12 | rd<<8 | ra<<4 )        X     #test str
	
	let imm = random(256);
	(movlop   <<12 | rd<<8 | imm )          (rd)  #test movl

end loop
end loop
end loop
*/

/* Test case RS1:
	INST                                    RS1  

let aluop  = 0b1000;
let ldrop  = 0b0101;
let strop  = 0b0100;
let movlop = 0b0000;

loop(rd, 1<<3)
loop(ra, 1<<3)
loop(rb, 1<<3)

loop(i, 4)
	((aluop+i)<<12 | rd<<8 | ra<<4 | rb<<0) (ra)  #test add/sub/and/orr
end loop

	(ldrop    <<12 | rd<<8 | ra<<4 )        (ra)  #test ldr
	(strop    <<12 | rd<<8 | ra<<4 )        (ra)  #test str

end loop
end loop
end loop
*/

/* Test case RS2:
	INST                                    RS2  

let aluop  = 0b1000;
let ldrop  = 0b0101;
let strop  = 0b0100;
let movlop = 0b0000;

loop(rd, 1<<3)
loop(ra, 1<<3)
loop(rb, 1<<3)

loop(i, 4)
	((aluop+i)<<12 | rd<<8 | ra<<4 | rb<<0) (rb) #test add/sub/and/orr
end loop
	(strop    <<12 | rd<<8 | ra<<4 )        (rd) #test str

end loop
end loop
end loop
*/

/* Test case STR:
	INST                                    STR 

let aluop  = 0b1000;
let ldrop  = 0b0101;
let strop  = 0b0100;
let movlop = 0b0000;

loop(rd, 1<<3)
loop(ra, 1<<3)
loop(rb, 1<<3)

loop(i, 4)
	((aluop+i)<<12 | rd<<8 | ra<<4 | rb<<0) 0  #test add/sub/and/orr
end loop

	(ldrop    <<12 | rd<<8 | ra<<4 )        0  #test ldr
	(strop    <<12 | rd<<8 | ra<<4 )        1  #test str
	
	let imm = random(256);
	(movlop   <<12 | rd<<8 | imm )          0  #test movl

end loop
end loop
end loop
*/

/* Test case WE:
	INST                                    WE  

let aluop  = 0b1000;
let ldrop  = 0b0101;
let strop  = 0b0100;
let movlop = 0b0000;

loop(rd, 1<<3)
loop(ra, 1<<3)
loop(rb, 1<<3)

loop(i, 4)
	((aluop+i)<<12 | rd<<8 | ra<<4 | rb<<0) 1  #test add/sub/and/orr
end loop

	(ldrop    <<12 | rd<<8 | ra<<4 )        1  #test ldr
	(strop    <<12 | rd<<8 | ra<<4 )        0  #test str
	
	let imm = random(256);
	(movlop   <<12 | rd<<8 | imm )          1  #test movl

end loop
end loop
end loop
*/

/* Test case LDR:
	INST                                    LDR 

let aluop  = 0b1000;
let ldrop  = 0b0101;
let strop  = 0b0100;
let movlop = 0b0000;

loop(rd, 1<<3)
loop(ra, 1<<3)
loop(rb, 1<<3)

loop(i, 4)
	((aluop+i)<<12 | rd<<8 | ra<<4 | rb<<0) X    #test add/sub/and/orr
end loop

	(ldrop    <<12 | rd<<8 | ra<<4 )        1    #test ldr
	(strop    <<12 | rd<<8 | ra<<4 )        X    #test str
	
	let imm = random(256);
	(movlop   <<12 | rd<<8 | imm )          X    #test movl

end loop
end loop
end loop
*/

/* Test case DMUX:
	INST                                    DMUX

let aluop  = 0b1000;
let ldrop  = 0b0101;
let strop  = 0b0100;
let movlop = 0b0000;

loop(rd, 1<<3)
loop(ra, 1<<3)
loop(rb, 1<<3)

loop(i, 4)
	((aluop+i)<<12 | rd<<8 | ra<<4 | rb<<0) 0  #test add/sub/and/orr
end loop

	(ldrop    <<12 | rd<<8 | ra<<4 )        1  #test ldr
	
	let imm = random(256);
	(movlop   <<12 | rd<<8 | imm )          2  #test movl

end loop
end loop
end loop
*/

/* Test case ALUOP:
	INST                                    ALUOP 

let aluop  = 0b1000;
let ldrop  = 0b0101;
let strop  = 0b0100;
let movlop = 0b0000;

loop(rd, 1<<3)
loop(ra, 1<<3)
loop(rb, 1<<3)

loop(i, 4)
	((aluop+i)<<12 | rd<<8 | ra<<4 | rb<<0) (i)    #test add/sub/and/orr
end loop

end loop
end loop
end loop
*/

/* Test case FLEN:
INST FLEN
loop(i, 16)
(i) (0)
end loop
(0b1000 << 12) (1)
(0b1001 << 12) (1)
(0b1010 << 12) (1)
(0b1011 << 12) (1)
(0b1111 << 12) (0)
*/

/* Test case SETH:
INST SETH
(0b0001 << 12) (1)
(0b1000 << 12) (0)
(0b1001 << 12) (0)
(0b1010 << 12) (0)
(0b1011 << 12) (0)
(0b1111 << 12) (0)
*/
